# Fritzing sketch rpiled-24-1 (saved by Fritzing 0.8.3b)
circuit board: 5.08238cm x 2.57732cm
breadboards: 1

parts:
  GRN = STP16NF06 N-Channel Power MOSFET
  BLU = STP16NF06 N-Channel Power MOSFET
  RED = STP16NF06 N-Channel Power MOSFET
  RGBO = female pin header, 4 pins [form="♀ (female)"]
  RGB = female pin header, 3 pins [form="♀ (female)"]
  RPi = Adafruit Pi Cobbler
  PWM = female pin header, 6 pins [form="♀ (female)"]
  V+ = female pin header, 3 pins [form="♀ (female)"]
  G+ = Resistor [tolerance=±5% resistance=1k package=THT]
  PWR = female pin header, 2 pins [form="♀ (female)"]
  R+ = Resistor [tolerance=±5% resistance=1k package=THT]
  B+ = Resistor [tolerance=±5% resistance=1k package=THT]

nets:
  N1: GRN.gate, RGB.pin2, G+.Pin_1
  N2: GRN.drain, RGBO.pin2
  N3: GRN.source, BLU.source, RED.source, RPi.PIN20, PWR.pin2
  N4: BLU.gate, RGB.pin3, B+.Pin_1
  N5: BLU.drain, RGBO.pin4
  N6: RED.gate, RGB.pin1, R+.Pin_1
  N7: RED.drain, RGBO.pin3
  N8: RGBO.pin1, PWR.pin1
  N9: RPi.3V3, PWM.pin1
  N10: RPi.GND, PWM.pin2
  N11: RPi.MOSI, PWM.pin3
  N12: RPi.SCLK, PWM.pin4
  N13: RPi.CE0, PWM.pin6
  N14: V+.pin1, R+.Pin_0
  N15: V+.pin2, G+.Pin_0
  N16: V+.pin3, B+.Pin_0

notes:
  These are pinheaders for the PWM. I am using an AdaFruit 24-channel 12-bit PWM (ID: 1429).
  12V
  This is the pinheader for the LED RGB flexistrip.
  NOTE: The MOSFET releases the Source when the Gate is HIGH. However, the 1429 turns the LEDs on when the voltage is LOW. Thus you may need to invert your software. 1 = OFF, and 0 = ON.
  Source: http://forums.adafruit.com/viewtopic.php?p=217512#p217512

custom parts:
  STP16NF06 N-Channel Power MOSFET: STP16NF06 N-channel Power MOSFET
  Adafruit Pi Cobbler: Adafruit Pi Cobbler GPIO Breakout for Raspberry Pi
